// Logisim project proj.circ as structural Verilog: 2 circuits, main circuit main
module main (
);

  wire and_1_out, and_2_out, and_3_out, and_4_out, clk, comparator_1_eq, comparator_2_eq, debugger_1_p1,
       iack, irq, kb_clear, kb_sel, mem, not_1_out, r_w, ram_sel, ter_sel, tim_sel, word;
  wire [0:0] kb_control;
  wire [5:0] int_v;
  wire [6:0] kb_sym;
  wire [15:0] addr, data, debugger_1_p5, debugger_1_p6, fp, pc, ps, r0, r1, r2, r3, r4, r5, r6, sp;

  // Probe on r0
  // Probe on fp
  Clock clock_1 (.out(clk));
  // Probe on r2
  // Probe on r1
  // Probe on pc
  // Probe on sp
  // CdM_16 cdm_16_1: pin names not known; wires that end beside it: irq, int_v, iack, r0, r1, r2, r3, r4, r5, r6, fp, pc, sp, ps, mem, r_w, word
  // Debugger debugger_1: pin names not known; wires that end beside it: debugger_1_p1, 1'b0, clk, addr, debugger_1_p5, debugger_1_p6
  // Probe on r4
  // Probe on r3
  // Probe on ps
  Keyboard keyboard_1 (.clk(clk), .re(kb_control[0]), .clr(kb_clear), .avail(irq), .data(kb_sym));
  Pull_Resistor pull_resistor_1 (.node(kb_control[0]));
  Pull_Resistor pull_resistor_2 (.node(kb_clear));
  // Probe on r6
  // Probe on r5
  assign data = not_1_out ? debugger_1_p5 : 16'bz;  // Controlled_Buffer controlled_buffer_1
  not not_1 (not_1_out, r_w);
  assign debugger_1_p6 = r_w ? data : 16'bz;  // Controlled_Buffer controlled_buffer_2
  // Probe on data
  // Probe on addr
  // Probe on data
  \interconnect  interconnect_1 (.addr(addr), .ram(ram_sel), .kb(kb_sel), .ter(ter_sel), .tim(tim_sel));
  Comparator #(.width(4), .mode("unsigned")) comparator_1 (
    .a(addr[3:0]), .b(4'b0000), .eq(comparator_1_eq));  // open: gt, lt
  Comparator #(.width(4), .mode("unsigned")) comparator_2 (
    .a(addr[3:0]), .b(4'b0001), .eq(comparator_2_eq));  // open: gt, lt
  assign int_v = irq ? 6'b000101 : 6'bz;  // Controlled_Buffer controlled_buffer_3
  and and_1 (and_1_out, comparator_1_eq, kb_sel);
  assign data[15:8] = and_2_out ? {{5{1'b0}}, kb_clear, irq, kb_control[0]} : 8'bz;  // Controlled_Buffer controlled_buffer_4
  and and_2 (and_2_out, comparator_1_eq, word, kb_sel);
  assign data[7:0] = and_3_out ? {{5{1'b0}}, kb_clear, irq, kb_control[0]} : 8'bz;  // Controlled_Buffer controlled_buffer_5
  and and_3 (and_3_out, comparator_2_eq, kb_sel);
  assign data[7:0] = and_1_out ? {1'b0, kb_sym} : 8'bz;  // Controlled_Buffer controlled_buffer_6
  Pull_Resistor pull_resistor_3 (.node(data[15:8]));
  TTY tty_1 (.clk(clk));  // open: data, we, clr
  and and_4 (and_4_out, mem, ram_sel);
  // RAM ram_1: pin names not known; wires that end beside it: debugger_1_p1, addr, word, and_4_out, clk, r_w, data

  // Other names for the same wires on the sheet: kb_next = kb_control[0]; kb_control[2:1] = {kb_clear, irq};
  //   kb_ready = irq

  // Notes on the sheet:
  //   Подай следующий!
  //   Очисти!
  //   Процессор
  //   Писать сюда :D
  //   Есть символ?
  //   Регистр состояния
  //   Устройства
  //   Клавиатура
  //   Регистр Символа
  //   Генерация Прерывания №5
  //   Отображение на память ;(
  //   Терминал
  //   Память
endmodule

module \interconnect  (
  input  [15:0] addr,
  output ram,
  output kb,
  output ter,
  output tim
);

  wire comparator_1_gt, comparator_2_eq, comparator_3_eq, comparator_4_gt, comparator_5_gt, comparator_6_eq,
       not_2_out, not_3_out;

  Comparator #(.width(4), .mode("unsigned")) comparator_1 (
    .a(addr[15:12]), .b(4'b1110), .gt(comparator_1_gt));  // open: eq, lt
  Comparator #(.width(4), .mode("unsigned")) comparator_2 (
    .a(addr[11:8]), .b(4'b0000), .eq(comparator_2_eq));  // open: gt, lt
  Comparator #(.width(4), .mode("unsigned")) comparator_3 (
    .a(addr[7:4]), .b(4'b0000), .eq(comparator_3_eq));  // open: gt, lt
  Comparator #(.width(4), .mode("unsigned")) comparator_4 (
    .a(addr[3:0]), .b(4'b0111), .gt(comparator_4_gt));  // open: eq, lt
  Comparator #(.width(4), .mode("unsigned")) comparator_5 (
    .a(addr[3:0]), .b(4'b1111), .gt(comparator_5_gt));  // open: eq, lt
  Comparator #(.width(4), .mode("unsigned")) comparator_6 (
    .a(addr[7:4]), .b(4'b0001), .eq(comparator_6_eq));  // open: gt, lt
  not not_1 (ram, comparator_1_gt);
  not not_2 (not_2_out, comparator_4_gt);
  not not_3 (not_3_out, comparator_5_gt);
  and and_1 (kb, comparator_1_gt, comparator_2_eq, comparator_3_eq, not_2_out);
  and and_2 (ter, comparator_1_gt, not_3_out, comparator_2_eq, comparator_4_gt, comparator_3_eq);
  and and_3 (tim, comparator_1_gt, comparator_6_eq, not_2_out, comparator_2_eq);

  // Notes on the sheet:
  //   0xF000-0xF007
  //   0xF008-0xF00F
endmodule
